# Fritzing sketch semaphore (saved by Fritzing 0.9.6b)
breadboards: 1

parts:
  Componente1 = Arduino Uno (Rev3)
  LED1 = smd LED [color="Red (633nm)" package="0603 [SMD]"]
  LED2 = smd LED [color="Yellow (595nm)" package="0603 [SMD]"]
  LED3 = smd LED [color="Green (560nm)" package="0603 [SMD]"]
  R1 = Resistor [tolerance=±5% resistance=220 package="2010 [SMD]"]
  R2 = Resistor [tolerance=±5% resistance=220 package="2010 [SMD]"]
  R3 = Resistor [tolerance=±5% resistance=220 package="2010 [SMD]"]

nets:
  N1: Componente1.D10_PWM/SS, R1.Pin_0
  N2: Componente1.D11_PWM/MOSI, R3.Pin_0
  N3: Componente1.D12/MISO, R2.Pin_0
  N4: Componente1.GND, LED1.anode, LED2.anode, LED3.anode
  N5: LED1.cathode, R2.Pin_1
  N6: LED2.cathode, R3.Pin_1
  N7: LED3.cathode, R1.Pin_1
