# Fritzing sketch schema (saved by Fritzing 0.9.6b)
breadboards: 1

parts:
  HC-SR04_Sensor_1 = HC-SR04 Ultrasonic Distance Sensor
  Keypad4x1 = Keypad Membran 4x4
  Componente1 = Arduino Uno (Rev3) - ICSP
  R1 = Resistor [tolerance=±5% resistance=220 package="1206 [SMD]"]
  LED1 = LED - 3mm [color="Green (565nm)" current=0.030 package="3 mm [THT]"]
  LED2 = LED - 3mm [color="Yellow (595nm)" current=0.030 package="3 mm [THT]"]
  LED3 = LED - 3mm [color="Red (633nm)" current=0.030 package="3 mm [THT]"]
  LED4 = LED - 3mm [color="Yellow (595nm)" current=0.030 package="3 mm [THT]"]
  LED5 = LED - 3mm [color="Green (565nm)" current=0.030 package="3 mm [THT]"]
  LED6 = LED - 3mm [color="Red (633nm)" current=0.030 package="3 mm [THT]"]
  R4 = Resistor [tolerance=±5% resistance=220 package="1206 [SMD]"]
  R5 = Resistor [tolerance=±5% resistance=220 package="1206 [SMD]"]
  R6 = Resistor [tolerance=±5% resistance=220 package="1206 [SMD]"]
  R7 = Resistor [tolerance=±5% resistance=220 package="1206 [SMD]"]
  R8 = Resistor [tolerance=±5% resistance=220 package="1206 [SMD]"]
  R9 = Resistor [tolerance=±5% resistance=220 package="1206 [SMD]"]

nets:
  VCC: HC-SR04_Sensor_1.VCC, Componente1.5V, R1.Pin_1
  N1: HC-SR04_Sensor_1.TRIG, Componente1.D10_PWM/SS
  N2: HC-SR04_Sensor_1.ECHO, Componente1.D9_PWM
  GND: HC-SR04_Sensor_1.GND, Keypad4x1.Pin4, Componente1.GND, LED1.anode, LED2.anode, LED3.anode, LED4.anode, LED5.anode, LED6.anode
  N3: Keypad4x1.Pin5, Componente1.D8, R1.Pin_0
  N4: Componente1.D2, R9.Pin_0
  N5: Componente1.D3_PWM, R8.Pin_0
  N6: Componente1.D4, R7.Pin_0
  N7: Componente1.D5_PWM, R6.Pin_0
  N8: Componente1.D6_PWM, R5.Pin_0
  N9: Componente1.D7, R4.Pin_0
  N10: LED1.cathode, R4.Pin_1
  N11: LED2.cathode, R5.Pin_1
  N12: LED3.cathode, R6.Pin_1
  N13: LED4.cathode, R8.Pin_1
  N14: LED5.cathode, R7.Pin_1
  N15: LED6.cathode, R9.Pin_1

custom parts:
  Keypad Membran 4x4: Membrane Keypad 4x4 Matrix
